# Fritzing sketch Main_Layout (saved by Fritzing 0.9.3b)
breadboards: 1

parts:
  Part1 = Adafruit HUZZAH ESP8266 [part_number="Adafruit #2471"]
  DHT1 = DHT11 Humitidy and Temperature Sensor
  VCC1 = Battery block 9V
  R1 = Resistor [tolerance=±5% resistance=10k package="2010 [SMD]"]
  U1 = Voltage Regulator - 5V [package="TO220 [THT]"]
  C3 = Electrolytic Capacitor [capacitance=1µF package="100 mil [THT, electrolytic]"]
  C4 = Capacitor Polarized [package=cpol-radial-100uf-25v]  # not connected
  J1 = Piezo Speaker

nets:
  GND: Part1.GND, DHT1.GND, VCC1.-, C3.+
  N1: Part1.VBAT, U1.input_voltage
  N2: Part1.GPIO2, DHT1.DATA, R1.Pin_1
  N3: Part1.GPIO4, J1.pin1
  N4: DHT1.VDD, R1.Pin_0
  N5: VCC1.+, U1.output_voltage
  N6: U1.GND, C3.-

custom parts:
  Adafruit HUZZAH ESP8266: Add Internet to your next project with an adorable, bite-sized WiFi microcontroller, at a price you like! The ESP8266 processor from Espressif is an 80 MHz microcontroller with a full WiFi front-end (both as client and access point) and TCP/IP stack with DNS support as well. While this chip has been very popular, its also been very difficult to use. Most of the low cost modules are not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
  DHT11 Humitidy and Temperature Sensor: DHT11 Humidity and Temperature Sensor
